# Fritzing sketch ethernet2.0 (saved by Fritzing 0.9.3b)

parts:
  J2 = Camdenboss CTB0158-4 [part_number=CTB0158-4 package=THT]
  Part1 = Arduino Uno (Rev3)
  J1 = Camdenboss CTB0158-4 [part_number=CTB0158-4 package=THT]
  R1 = Resistor [tolerance=±5% resistance=220 package=THT]  # not connected
  R2 = Resistor [tolerance=±5% resistance=220 package=THT]  # not connected

nets:
  N1: J2.terminal_1, Part1.D12/MISO
  N2: J2.terminal_2, Part1.D13/SCK
  N3: J2.terminal_4, Part1.GND
  N4: Part1.D10_PWM/SS, J1.terminal_3
  N5: Part1.D11_PWM/MOSI, J1.terminal_2
  N6: Part1.3V3, J1.terminal_4

notes:
  3.3v
  Ground
  HanRun Ethernet shield.
