# Fritzing sketch project (saved by Fritzing 0.9.3b)
breadboards: 1

parts:
  J2 = Camdenboss CTB0158-4 [part_number=CTB0158-4 package=THT]
  Part1 = Arduino Uno (Rev3)
  J1 = Camdenboss CTB0158-4 [part_number=CTB0158-4 package=THT]
  R1 = Resistor [tolerance=±5% resistance=220 package=THT]  # not connected
  R2 = Resistor [tolerance=±5% resistance=220 package=THT]  # not connected
  J3 = Piezo Speaker
  Part2 = Humidity Temperature Sensor SHT15  # not connected
  RHT1 = Humidity and Temperature Sensor RHT03  # not connected
  J4 = Camdenboss CTB0158-3 [part_number=CTB0158-3 package=THT]
  R3 = Resistor [tolerance=±5% resistance=220 package=THT]
  U1 = GAS_SENSOR [package=mq-3]  # not connected
  R4 = Resistor [tolerance=±5% resistance=220 package=THT]
  J6 = Camdenboss CTB0158-4 [part_number=CTB0158-4 package=THT]
  R5 = Resistor [tolerance=±5% resistance=220 package=THT]  # not connected
  R6 = Resistor [tolerance=±5% resistance=220 package=THT]  # not connected

nets:
  N1: J2.terminal_1, Part1.D12/MISO
  N2: J2.terminal_2, Part1.D13/SCK
  N3: J2.terminal_4, Part1.GND
  N4: Part1.A0, J6.pin1
  N5: Part1.D9_PWM, J3.pin2
  N6: Part1.D10_PWM/SS, J1.terminal_3
  N7: Part1.D11_PWM/MOSI, J1.terminal_2
  N8: Part1.D2, R3.Pin_1
  N9: Part1.3V3, J1.terminal_4
  N10: Part1.5V, R4.Pin_1, J6.pin3
  N11: J3.pin1, J4.pin2, J4.terminal_2
  N12: J4.pin1, J4.terminal_1
  N13: J4.pin3, J4.terminal_3, R3.Pin_0
  N14: R4.Pin_0, J6.pin4

notes:
  3.3v
  Ground
  HanRun Ethernet shield.
